// Logisim project mdnf.circ as structural Verilog: 1 circuit, main circuit mdnf
module mdnf (
);

  wire and_1_out, and_2_out, and_3_out, and_4_out, and_5_out, and_6_out, and_7_out, and_8_out, not_1_out,
       not_2_out, not_3_out, not_4_out, not_5_out, not_6_out, not_7_out, not_8_out, or_1_out, or_2_out,
       or_3_out, x0_out, x1_out, x2_out, x3_out;

  Clock x3 (.out(x3_out));
  Clock x2 (.out(x2_out));
  Clock x1 (.out(x1_out));
  Clock x0 (.out(x0_out));
  not not_1 (not_1_out, x3_out);
  and and_1 (and_1_out, not_1_out, not_2_out);
  not not_2 (not_2_out, x1_out);
  not not_3 (not_3_out, x0_out);
  not not_4 (not_4_out, x2_out);
  not not_5 (not_5_out, x0_out);
  not not_6 (not_6_out, x3_out);
  and and_2 (and_2_out, not_6_out, x2_out);
  and and_3 (and_3_out, x1_out, x0_out);
  and and_4 (and_4_out, x3_out, not_7_out);
  not not_7 (not_7_out, x2_out);
  not not_8 (not_8_out, x1_out);
  and and_5 (and_5_out, and_1_out, not_3_out);
  and and_6 (and_6_out, not_4_out, not_5_out);
  and and_7 (and_7_out, and_2_out, and_3_out);
  and and_8 (and_8_out, and_4_out, not_8_out);
  or or_1 (or_1_out, and_5_out, and_6_out);
  or or_2 (or_2_out, and_7_out, and_8_out);
  LED led_1 (.in(or_3_out));
  or or_3 (or_3_out, or_1_out, or_2_out);
endmodule
