// Logisim project HW-02.circ as structural Verilog: 3 circuits, main circuit main
module main (
);

  wire and_1_out, and_2_out, and_3_out, and_4_out, and_5_out, and_6_out, and_7_out, and_8_out, minus_1_out,
       or_1_out, or_2_out, or_3_out, or_4_out, or_5_out, or_6_out, or_7_out, or_8_out, or_9_out, plus_1_out,
       s_r_ff_1_q, s_r_ff_2_q, t_trigger_1_nq, t_trigger_1_q, t_trigger_2_nq, t_trigger_2_q, t_trigger_3_nq,
       t_trigger_3_q, t_trigger_4_nq, t_trigger_4_q;

  Clock plus_1 (.out(plus_1_out));
  Clock #(.highDuration(100), .lowDuration(100)) minus_1 (.out(minus_1_out));
  or or_1 (or_1_out, plus_1_out, minus_1_out);
  T_trigger t_trigger_1 (.C(or_1_out), .R(or_2_out), .Q(t_trigger_1_q), .nQ(t_trigger_1_nq));
  or or_2 (or_2_out, s_r_ff_2_q, s_r_ff_1_q);
  and and_1 (and_1_out, plus_1_out, t_trigger_1_q);
  and and_2 (and_2_out, t_trigger_1_nq, minus_1_out);
  LED Q0 (.in(t_trigger_1_q));
  or or_3 (or_3_out, and_1_out, and_2_out);
  T_trigger t_trigger_2 (.C(or_3_out), .R(s_r_ff_1_q), .Q(t_trigger_2_q), .nQ(t_trigger_2_nq));
  LED Q1 (.in(t_trigger_2_q));
  and and_3 (and_3_out, plus_1_out, t_trigger_1_q, t_trigger_2_q);
  or or_4 (or_4_out, and_3_out, and_4_out);
  and and_4 (and_4_out, t_trigger_2_nq, t_trigger_1_nq, minus_1_out);
  or or_5 (or_5_out, s_r_ff_2_q, s_r_ff_1_q);
  T_trigger t_trigger_3 (.C(or_4_out), .R(or_5_out), .Q(t_trigger_3_q), .nQ(t_trigger_3_nq));
  LED Q2 (.in(t_trigger_3_q));
  and and_5 (and_5_out, plus_1_out, t_trigger_1_q, t_trigger_2_q, t_trigger_3_q);
  or or_6 (or_6_out, and_5_out, and_6_out);
  and and_6 (and_6_out, t_trigger_3_nq, t_trigger_2_nq, t_trigger_1_nq, minus_1_out);
  T_trigger t_trigger_4 (.C(or_6_out), .R(s_r_ff_1_q), .Q(t_trigger_4_q), .nQ(t_trigger_4_nq));
  LED Q3 (.in(t_trigger_4_q));
  and and_7 (and_7_out, t_trigger_1_q, t_trigger_2_q, ~t_trigger_3_q, t_trigger_4_q);  // AND_Gate
  or or_7 (or_7_out, plus_1_out, minus_1_out);
  and and_8 (and_8_out, ~t_trigger_4_nq, ~t_trigger_3_nq, ~t_trigger_2_nq, ~t_trigger_1_nq);  // AND_Gate
  or or_8 (or_8_out, and_7_out, or_7_out);
  or or_9 (or_9_out, and_8_out, or_7_out);
  S_R_Flip_Flop s_r_ff_1 (.S(and_7_out), .clk(or_8_out), .R(or_7_out), .Q(s_r_ff_1_q));  // open: Qn, preset, reset, en
  S_R_Flip_Flop s_r_ff_2 (.S(and_8_out), .clk(or_9_out), .R(or_7_out), .Q(s_r_ff_2_q));  // open: Qn, preset, reset, en
endmodule

module RS_trigger (
  input  S,
  input  C,
  input  R,
  output Q,
  output nQ
);

  wire nand_1_out, nand_2_out;

  nand nand_1 (nand_1_out, S, C);
  nand nand_2 (nand_2_out, C, R);
  nand nand_3 (Q, nand_1_out, nQ);
  nand nand_4 (nQ, Q, nand_2_out);
endmodule

// T
module T_trigger (
  input  C,
  input  R,
  output Q,
  output nQ
);

  wire nand_1_out, nand_2_out, nand_3_out, nand_4_out, nand_5_out, nand_6_out, not_1_out, not_2_out;

  not not_1 (not_1_out, R);
  nand nand_1 (nand_1_out, nQ, 1'b1, C);
  nand nand_2 (nand_2_out, C, 1'b1, Q);
  not not_2 (not_2_out, C);
  nand nand_3 (nand_3_out, 1'b1, nand_1_out, nand_4_out);
  nand nand_4 (nand_4_out, nand_3_out, nand_2_out, not_1_out);
  nand nand_5 (nand_5_out, nand_3_out, not_2_out);
  nand nand_6 (nand_6_out, nand_4_out, not_2_out);
  nand nand_7 (Q, 1'b1, nand_5_out, nQ);
  nand nand_8 (nQ, Q, nand_6_out, not_1_out);
endmodule
